// Logisim project cpu32.circ as structural Verilog: 7 circuits, main circuit reg2mux
module main (
);

  wire alu_1_carryout, and_1_out, and_2_out, and_3_out, and_4_out, CFLAG, clock_1_out, comparator_1_eq,
       comparator_2_eq, comparator_3_eq, comparator_4_eq, comparator_5_eq, comparator_6_eq, comparator_7_eq,
       comparator_8_eq, comparator_9_eq, comparator_10_eq, comparator_12_eq, comparator_13_eq, not_1_out,
       not_2_out, or_1_out, or_2_out, or_3_out, OUTCARRYUPDATE;
  wire [1:0] instructiondecoder_1_outop;
  wire [2:0] OUTBC;
  wire [3:0] demultiplexer_2_out0, FLAGSIN, instructiondecoder_1_outr0, instructiondecoder_1_outr1,
       multiplexer_3_out, multiplexer_4_out, OUTALUOP;
  wire [6:0] reg2mux_1_out0_4;
  wire [7:0] FLAGSOUT, multiplexer_5_out, OUTOPCODE, ram32_1_out0, ram32_1_out1, ram32_1_out2, ram32_1_out3,
       reg2mux_1_out0, reg2mux_1_out0_2, reg2mux_1_out0_3;
  wire [15:0] demultiplexer_1_out0, instructiondecoder_1_outimm, multiplexer_7_out;
  wire [16:0] bitselector_1_out, counter_1_q;
  wire [23:0] adder_1_out, bit_extender_1_out, bitselector_2_out;
  wire [31:0] alu_1_out0, bit_extender_2_out, bit_extender_3_out, bit_extender_4_out, bit_extender_5_out,
       bit_extender_6_out, multiplexer_2_out, multiplexer_6_out, multiplexer_8_out, multiplexer_9_out,
       reg2mux_1_out1, registerfile_1_r0out, registerfile_1_r1out, registerfile_1_r2out,
       registerfile_1_r3out, registerfile_1_r4out, registerfile_1_r5out, registerfile_1_r6out,
       registerfile_1_r7out, registerfile_1_r8out, registerfile_1_r9out, registerfile_1_r10out,
       registerfile_1_r11out, registerfile_1_r12out, registerfile_1_r13out, registerfile_1_r14out,
       registerfile_1_r15out, rom_1_data;

  instructionDecoder instructiondecoder_1 (
    .IN0(rom_1_data), .OUTOP(instructiondecoder_1_outop), .OUTR0(instructiondecoder_1_outr0),
    .OUTIMM(instructiondecoder_1_outimm), .OUTR1(instructiondecoder_1_outr1), .OUTOPCODE(OUTOPCODE),
    .OUTALUOP(OUTALUOP), .OUTBC(OUTBC), .OUTCARRYUPDATE(OUTCARRYUPDATE));
  Comparator #(.width(2)) comparator_1 (
    .a(instructiondecoder_1_outop), .b(2'b00), .eq(comparator_1_eq));  // open: gt, lt
  Comparator #(.width(2)) comparator_2 (
    .a(instructiondecoder_1_outop), .b(2'b01), .eq(comparator_2_eq));  // open: gt, lt
  Comparator #(.width(2)) comparator_3 (
    .a(instructiondecoder_1_outop), .b(2'b11), .eq(comparator_3_eq));  // open: gt, lt
  Comparator comparator_4 (.a(OUTOPCODE), .b(8'h5), .eq(comparator_4_eq));  // open: gt, lt
  or or_1 (or_1_out, comparator_1_eq, comparator_2_eq);
  and and_1 (and_1_out, comparator_3_eq, comparator_4_eq);
  Comparator comparator_5 (.a(OUTOPCODE), .b(8'h6), .eq(comparator_5_eq));  // open: gt, lt
  or or_2 (or_2_out, or_1_out, and_1_out);
  and and_2 (and_2_out, comparator_5_eq, not_1_out);
  not not_1 (not_1_out, FLAGSOUT[0]);
  Demultiplexer #(.enable("true"), .select(4)) demultiplexer_1 (
    .out0(demultiplexer_1_out0[0]), .out1(demultiplexer_1_out0[1]), .out2(demultiplexer_1_out0[2]),
    .out3(demultiplexer_1_out0[3]), .out4(demultiplexer_1_out0[4]), .out5(demultiplexer_1_out0[5]),
    .out6(demultiplexer_1_out0[6]), .out7(demultiplexer_1_out0[7]), .out8(demultiplexer_1_out0[8]),
    .out9(demultiplexer_1_out0[9]), .out10(demultiplexer_1_out0[10]), .out11(demultiplexer_1_out0[11]),
    .out12(demultiplexer_1_out0[12]), .out13(demultiplexer_1_out0[13]), .out14(demultiplexer_1_out0[14]),
    .out15(demultiplexer_1_out0[15]), .in(1'b1), .sel(instructiondecoder_1_outr0), .en(and_3_out));
  not not_2 (not_2_out, comparator_6_eq);
  Comparator comparator_6 (.a(OUTOPCODE), .b({8{1'b0}}), .eq(comparator_6_eq));  // open: gt, lt
  BitSelector #(.group(17), .width(32)) bitselector_1 (
    .in({FLAGSIN[1], reg2mux_1_out0_4, reg2mux_1_out0_3, reg2mux_1_out0_2, reg2mux_1_out0}),
    .out(bitselector_1_out), .sel(1'b0));
  Counter #(.max('h1ffff), .width(17)) counter_1 (
    .load(and_2_out), .up(1'b1), .count(1'b1), .clk(clock_1_out), .D(bitselector_1_out), .Q(counter_1_q));  // open: clr, carry
  and and_3 (and_3_out, not_2_out, or_2_out);
  Clock clock_1 (.out(clock_1_out));
  flags flags_1 (
    .INOP(instructiondecoder_1_outop), .IN0({4'b0000, FLAGSIN}), .CLK(clock_1_out),
    .OUT0({FLAGSOUT[7:3], CFLAG, FLAGSOUT[1:0]}));
  ROM #(.addrWidth(17), .dataWidth(32)) rom_1 (.addr(counter_1_q), .data(rom_1_data));
  registerFile registerfile_1 (
    .WE(demultiplexer_1_out0), .CLK(clock_1_out), .IN0(multiplexer_2_out), .R0OUT(registerfile_1_r0out),
    .R1OUT(registerfile_1_r1out), .R2OUT(registerfile_1_r2out), .R3OUT(registerfile_1_r3out),
    .R4OUT(registerfile_1_r4out), .R5OUT(registerfile_1_r5out), .R6OUT(registerfile_1_r6out),
    .R7OUT(registerfile_1_r7out), .R8OUT(registerfile_1_r8out), .R9OUT(registerfile_1_r9out),
    .R10OUT(registerfile_1_r10out), .R11OUT(registerfile_1_r11out), .R12OUT(registerfile_1_r12out),
    .R13OUT(registerfile_1_r13out), .R14OUT(registerfile_1_r14out), .R15OUT(registerfile_1_r15out));
  Comparator comparator_7 (.a(OUTOPCODE), .b(8'h7), .eq(comparator_7_eq));  // open: gt, lt
  Comparator comparator_8 (.a(OUTOPCODE), .b(8'h8), .eq(comparator_8_eq));  // open: gt, lt
  or or_3 (or_3_out, comparator_7_eq, comparator_8_eq);
  reg2mux reg2mux_1 (
    .R0(registerfile_1_r0out), .R1(registerfile_1_r1out), .R2(registerfile_1_r2out),
    .R3(registerfile_1_r3out), .R4(registerfile_1_r4out), .R5(registerfile_1_r5out),
    .R6(registerfile_1_r6out), .R7(registerfile_1_r7out), .R8(registerfile_1_r8out),
    .R9(registerfile_1_r9out), .R10(registerfile_1_r10out), .R11(registerfile_1_r11out),
    .R12(registerfile_1_r12out), .R13(registerfile_1_r13out), .R14(registerfile_1_r14out),
    .R15(registerfile_1_r15out), .SEL0(instructiondecoder_1_outr0), .SEL1(instructiondecoder_1_outr1),
    .OUT0({FLAGSIN[1], reg2mux_1_out0_4, reg2mux_1_out0_3, reg2mux_1_out0_2, reg2mux_1_out0}),
    .OUT1(reg2mux_1_out1));
  and and_4 (and_4_out, CFLAG, or_3_out);
  BitSelector #(.group(24), .width(32)) bitselector_2 (.in(reg2mux_1_out1), .out(bitselector_2_out), .sel(1'b0));
  Multiplexer multiplexer_1 (.in0(CFLAG), .in1(alu_1_carryout), .out(FLAGSIN[2]), .sel(OUTCARRYUPDATE));
  alu alu_1 (
    .CARRYIN(and_4_out),
    .REG0({FLAGSIN[1], reg2mux_1_out0_4, reg2mux_1_out0_3, reg2mux_1_out0_2, reg2mux_1_out0}),
    .REG1(reg2mux_1_out1), .OPSEL(OUTALUOP), .IMM16(instructiondecoder_1_outimm), .OUT0(alu_1_out0),
    .CARRYOUT(alu_1_carryout), .OVERFLOWOUT(FLAGSIN[3]));
  assign bit_extender_1_out = {{8{instructiondecoder_1_outimm[15]}}, instructiondecoder_1_outimm};  // Bit_Extender bit_extender_1
  assign bit_extender_2_out = {{16{1'b0}}, instructiondecoder_1_outimm};  // Bit_Extender bit_extender_2
  Comparator #(.width(2)) comparator_9 (
    .a(instructiondecoder_1_outop), .b(2'b01), .eq(comparator_9_eq));  // open: gt, lt
  Comparator #(.width(2)) comparator_10 (
    .a(instructiondecoder_1_outop), .b(2'b10), .eq(comparator_10_eq));  // open: gt, lt
  Multiplexer #(.select(2), .width(32)) multiplexer_2 (
    .in0(alu_1_out0), .in1(multiplexer_9_out), .in2({32{1'b0}}), .in3(bit_extender_2_out),
    .out(multiplexer_2_out), .sel(instructiondecoder_1_outop));
  Adder #(.width(24)) adder_1 (
    .a(bit_extender_1_out), .b(bitselector_2_out), .out(adder_1_out), .cin(1'b0));  // open: cout
  Demultiplexer #(.select(2)) demultiplexer_2 (
    .out0(demultiplexer_2_out0[0]), .out1(demultiplexer_2_out0[1]), .out2(demultiplexer_2_out0[2]),
    .out3(demultiplexer_2_out0[3]), .in(1'b1), .sel(adder_1_out[1:0]));
  Comparator #(.width(32)) comparator_11 (.a(alu_1_out0), .b({32{1'b0}}), .eq(FLAGSIN[0]));  // open: gt, lt
  Multiplexer #(.enable("true"), .select(3), .width(4)) multiplexer_3 (
    .in0(4'b0000), .in1(demultiplexer_2_out0), .in2(multiplexer_4_out), .in3(4'b0000), .in4(4'b1111),
    .in5(4'b0000), .in6(4'b0000), .in7(4'b0000), .out(multiplexer_3_out), .sel(OUTBC), .en(comparator_10_eq));
  Multiplexer #(.width(4)) multiplexer_4 (.in0(4'b0011), .in1(4'b1100), .out(multiplexer_4_out), .sel(adder_1_out[1]));
  ram32 ram32_1 (
    .IN0(reg2mux_1_out0), .IN1(reg2mux_1_out0_2), .IN2(reg2mux_1_out0_3),
    .IN3({FLAGSIN[1], reg2mux_1_out0_4}), .ADDR(adder_1_out[23:2]), .WRITE(multiplexer_3_out),
    .READ(4'b1111), .CLK(clock_1_out), .OUT0(ram32_1_out0), .OUT1(ram32_1_out1), .OUT2(ram32_1_out2),
    .OUT3(ram32_1_out3));
  Multiplexer #(.select(2), .width(8)) multiplexer_5 (
    .in0(ram32_1_out0), .in1(ram32_1_out1), .in2(ram32_1_out2), .in3(ram32_1_out3), .out(multiplexer_5_out),
    .sel(adder_1_out[1:0]));
  Multiplexer #(.width(32)) multiplexer_6 (
    .in0(bit_extender_6_out), .in1(bit_extender_5_out), .out(multiplexer_6_out), .sel(comparator_12_eq));
  Multiplexer #(.width(16)) multiplexer_7 (
    .in0({ram32_1_out1, ram32_1_out0}), .in1({ram32_1_out3, ram32_1_out2}), .out(multiplexer_7_out),
    .sel(adder_1_out[1]));
  Comparator comparator_12 (.a(OUTOPCODE), .b(8'hc), .eq(comparator_12_eq));  // open: gt, lt
  Comparator comparator_13 (.a(OUTOPCODE), .b(8'he), .eq(comparator_13_eq));  // open: gt, lt
  assign bit_extender_3_out = {{24{1'b0}}, multiplexer_5_out};  // Bit_Extender bit_extender_3
  assign bit_extender_4_out = {{24{multiplexer_5_out[7]}}, multiplexer_5_out};  // Bit_Extender bit_extender_4
  assign bit_extender_5_out = {{16{1'b0}}, multiplexer_7_out};  // Bit_Extender bit_extender_5
  assign bit_extender_6_out = {{16{multiplexer_7_out[15]}}, multiplexer_7_out};  // Bit_Extender bit_extender_6
  Multiplexer #(.width(32)) multiplexer_8 (
    .in0(bit_extender_4_out), .in1(bit_extender_3_out), .out(multiplexer_8_out), .sel(comparator_13_eq));
  Multiplexer #(.enable("true"), .select(3), .width(32)) multiplexer_9 (
    .in0({32{1'b0}}), .in1(multiplexer_8_out), .in2(multiplexer_6_out), .in3({32{1'b0}}),
    .in4({ram32_1_out3, ram32_1_out2, ram32_1_out1, ram32_1_out0}), .in5({32{1'b0}}), .in6({32{1'b0}}),
    .in7({32{1'b0}}), .out(multiplexer_9_out), .sel(OUTBC), .en(comparator_9_eq));

  // Other names for the same wires on the sheet: ZFLAG = FLAGSOUT[0]; NFLAG = FLAGSOUT[1]; FLAGSOUT[2] = CFLAG;
  //   OFLAG = FLAGSOUT[3]

  // Notes on the sheet:
  //   only write to registers if the current instruction requires it
  //   don't write if the current instruction is =0(nop)
  //   contents of rom_1 (hex, n*v repeats v):
  //   60105 430205 62101 40104 f0205 f0305 3202 40d03 6 7fff0109 ffff010a 40104 40503 4020e 5030e 6040e
  //   ff0618 1712 800117 3111 113 12340105 40119 205 80000209 10219 12340305 4031a f0405 1041a ffff0509
  //   8000050a 40d05 d516
  //   byte offset
  //   word addr
  //   flags0=zero,1=negative,2=carry/borrow
  //   zero extend for LWU
  //   zero extend for LBU
endmodule

module reg2mux (
  input  [31:0] R0,
  input  [31:0] R1,
  input  [31:0] R2,
  input  [31:0] R3,
  input  [31:0] R4,
  input  [31:0] R5,
  input  [31:0] R6,
  input  [31:0] R7,
  input  [31:0] R8,
  input  [31:0] R9,
  input  [31:0] R10,
  input  [31:0] R11,
  input  [31:0] R12,
  input  [31:0] R13,
  input  [31:0] R14,
  input  [31:0] R15,
  input  [3:0] SEL0,
  input  [3:0] SEL1,
  output [31:0] OUT0,
  output [31:0] OUT1
);

  Multiplexer #(.select(4), .width(32)) multiplexer_1 (
    .in0(R0), .in1(R1), .in2(R2), .in3(R3), .in4(R4), .in5(R5), .in6(R6), .in7(R7), .in8(R8), .in9(R9),
    .in10(R10), .in11(R11), .in12(R12), .in13(R13), .in14(R14), .in15(R15), .out(OUT0), .sel(SEL0));
  Multiplexer #(.select(4), .width(32)) multiplexer_2 (
    .in0(R0), .in1(R1), .in2(R2), .in3(R3), .in4(R4), .in5(R5), .in6(R6), .in7(R7), .in8(R8), .in9(R9),
    .in10(R10), .in11(R11), .in12(R12), .in13(R13), .in14(R14), .in15(R15), .out(OUT1), .sel(SEL1));
endmodule

module alu (
  input  CARRYIN,
  input  [31:0] REG0,
  input  [31:0] REG1,
  input  [3:0] OPSEL,
  input  [15:0] IMM16,
  output [31:0] OUT0,
  output CARRYOUT,
  output OVERFLOWOUT
);

  wire adder_1_cout, adder_2_cout, bitselector_3_out, bitselector_4_out, bitselector_5_out,
       bitselector_6_out, bitselector_7_out, comparator_1_eq, comparator_2_eq, comparator_3_eq,
       comparator_4_eq, comparator_5_eq, multiplexer_5_out, not_2_out, not_3_out, or_1_out,
       subtractor_3_bout, subtractor_4_bout, xor_2_out, xor_3_out;
  wire [4:0] bitselector_1_out, bitselector_2_out, subtractor_2_out;
  wire [7:0] bit_extender_1_out, subtractor_1_out;
  wire [31:0] adder_1_out, adder_2_out, and_1_out, bit_extender_2_out, bit_extender_3_out, multiplexer_1_out,
       multiplexer_2_out, multiplexer_3_out, multiplexer_4_out, not_1_out, or_2_out, shifter_1_out,
       shifter_2_out, shifter_3_out, subtractor_3_out, subtractor_4_out, xor_1_out;

  Comparator #(.width(4)) comparator_1 (.a(OPSEL), .b(4'b1001), .eq(comparator_1_eq));  // open: gt, lt
  Comparator #(.width(4)) comparator_2 (.a(OPSEL), .b(4'b1011), .eq(comparator_2_eq));  // open: gt, lt
  Multiplexer #(.width(32)) multiplexer_1 (
    .in0(REG1), .in1(bit_extender_3_out), .out(multiplexer_1_out), .sel(or_1_out));
  or or_1 (or_1_out, comparator_1_eq, comparator_2_eq);
  Comparator #(.width(4)) comparator_3 (.a(OPSEL), .b(4'b0100), .eq(comparator_3_eq));  // open: gt, lt
  Comparator #(.width(4)) comparator_4 (.a(OPSEL), .b(4'b0110), .eq(comparator_4_eq));  // open: gt, lt
  BitSelector #(.group(5), .width(32)) bitselector_1 (.in(multiplexer_1_out), .out(bitselector_1_out), .sel(3'b000));
  Multiplexer #(.width(32)) multiplexer_2 (
    .in0(REG1), .in1(bit_extender_3_out), .out(multiplexer_2_out), .sel(comparator_3_eq));
  Multiplexer #(.width(32)) multiplexer_3 (
    .in0(REG1), .in1(bit_extender_3_out), .out(multiplexer_3_out), .sel(comparator_4_eq));
  assign not_1_out = ~REG0;  // NOT_Gate not_1, 32 bits wide
  Shifter #(.width(32)) shifter_1 (.in(REG0), .\dist (bitselector_1_out), .out(shifter_1_out));
  Shifter #(.shift("lr"), .width(32)) shifter_2 (.in(REG0), .\dist (bitselector_1_out), .out(shifter_2_out));
  Shifter #(.shift("ar"), .width(32)) shifter_3 (.in(REG0), .\dist (bitselector_1_out), .out(shifter_3_out));
  assign and_1_out = multiplexer_2_out & REG0;  // AND_Gate and_1, 32 bits wide
  assign xor_1_out = multiplexer_3_out ^ REG0;  // XOR_Gate xor_1, 32 bits wide
  assign bit_extender_1_out = {{3{1'b0}}, bitselector_1_out};  // Bit_Extender bit_extender_1
  Subtractor subtractor_1 (.a(8'h20), .b(bit_extender_1_out), .out(subtractor_1_out), .bin(1'b0));  // open: bout
  Subtractor #(.width(5)) subtractor_2 (
    .a(bitselector_1_out), .b(5'b00001), .out(subtractor_2_out), .bin(1'b0));  // open: bout
  BitSelector #(.group(5)) bitselector_2 (.in(subtractor_1_out), .out(bitselector_2_out), .sel(1'b0));
  BitSelector #(.width(32)) bitselector_3 (.in(REG0), .out(bitselector_3_out), .sel(subtractor_2_out));
  assign or_2_out = REG0 | bit_extender_3_out;  // OR_Gate or_2, 32 bits wide
  BitSelector #(.width(32)) bitselector_4 (.in(REG0), .out(bitselector_4_out), .sel(bitselector_2_out));
  assign bit_extender_2_out = {{16{IMM16[15]}}, IMM16};  // Bit_Extender bit_extender_2
  assign bit_extender_3_out = {{16{1'b0}}, IMM16};  // Bit_Extender bit_extender_3
  BitSelector #(.width(32)) bitselector_5 (.in(bit_extender_2_out), .out(bitselector_5_out), .sel({5{1'b1}}));
  Adder #(.width(32)) adder_1 (.a(REG0), .b(REG1), .out(adder_1_out), .cin(CARRYIN), .cout(adder_1_cout));
  Subtractor #(.width(32)) subtractor_3 (
    .a(REG0), .b(REG1), .out(subtractor_3_out), .bin(CARRYIN), .bout(subtractor_3_bout));
  BitSelector #(.width(32)) bitselector_6 (.in(multiplexer_4_out), .out(bitselector_6_out), .sel({5{1'b1}}));
  Adder #(.width(32)) adder_2 (
    .a(adder_1_out), .b(bit_extender_2_out), .out(adder_2_out), .cin(adder_1_cout), .cout(adder_2_cout));
  Subtractor #(.width(32)) subtractor_4 (
    .a(subtractor_3_out), .b(bit_extender_2_out), .out(subtractor_4_out), .bin(subtractor_3_bout),
    .bout(subtractor_4_bout));
  Multiplexer #(.width(32)) multiplexer_4 (
    .in0(adder_1_out), .in1(subtractor_3_out), .out(multiplexer_4_out), .sel(not_3_out));
  xor xor_2 (xor_2_out, bitselector_6_out, bitselector_5_out);
  not not_2 (not_2_out, xor_2_out);
  BitSelector #(.width(32)) bitselector_7 (.in(adder_2_out), .out(bitselector_7_out), .sel({5{1'b1}}));
  xor xor_3 (xor_3_out, bitselector_7_out, bitselector_6_out);
  and and_2 (OVERFLOWOUT, xor_3_out, multiplexer_5_out);
  Multiplexer multiplexer_5 (.in0(not_2_out), .in1(xor_2_out), .out(multiplexer_5_out), .sel(not_3_out));
  Comparator #(.width(4)) comparator_5 (.a(OPSEL), .b(4'b0000), .eq(comparator_5_eq));  // open: gt, lt
  Multiplexer #(.select(4), .width(32)) multiplexer_6 (
    .in0(adder_2_out), .in1(subtractor_4_out), .in2({IMM16, {16{1'b0}}}), .in3(or_2_out), .in4(and_1_out),
    .in5(and_1_out), .in6(xor_1_out), .in7(xor_1_out), .in8(not_1_out), .in9(shifter_1_out),
    .in10(shifter_1_out), .in11(shifter_2_out), .in12(shifter_2_out), .in13(shifter_3_out),
    .in14({32{1'b0}}), .in15({32{1'b0}}), .out(OUT0), .sel(OPSEL));
  not not_3 (not_3_out, comparator_5_eq);
  Multiplexer #(.select(4)) multiplexer_7 (
    .in0(adder_2_cout), .in1(subtractor_4_bout), .in2(1'b0), .in3(1'b0), .in4(1'b0), .in5(1'b0), .in6(1'b0),
    .in7(1'b0), .in8(1'b0), .in9(bitselector_4_out), .in10(bitselector_4_out), .in11(bitselector_3_out),
    .in12(bitselector_3_out), .in13(bitselector_3_out), .in14(1'b0), .in15(1'b0), .out(CARRYOUT), .sel(OPSEL));

  // Notes on the sheet:
  //   if op == shli or shri, use immediate
  //   andi/and
  //   xori/xor
  //   not
  //   shli,shl,shri,shr,sar
  //   ori
  //   left shift carry
  //   right shift carry
  //   add
  //   sub
  //   lui
  //   add=0,sub=1
endmodule

module instructionDecoder (
  input  [31:0] IN0,
  output [1:0] OUTOP,
  output [3:0] OUTR0,
  output [15:0] OUTIMM,
  output [3:0] OUTR1,
  output [7:0] OUTOPCODE,
  output [3:0] OUTALUOP,
  output [2:0] OUTBC,
  output OUTCARRYUPDATE
);

  ROM #(.dataWidth(2)) rom_1 (.addr(IN0[7:0]), .data(OUTOP));
  ROM #(.dataWidth(4)) rom_2 (.addr(IN0[7:0]), .data(OUTALUOP));
  ROM #(.dataWidth(3)) rom_3 (.addr(IN0[7:0]), .data(OUTBC));
  ROM #(.dataWidth(1)) rom_4 (.addr(IN0[7:0]));  // open: data

  assign OUTIMM = IN0[31:16];
  assign OUTOPCODE = IN0[7:0];
  assign OUTR0 = IN0[11:8];
  assign OUTR1 = IN0[15:12];

  // Notes on the sheet:
  //   contents of rom_1 (hex, n*v repeats v):
  //   0 0 0 1 2 3 3 4*0 4*1 2 2
  //   contents of rom_2 (hex, n*v repeats v):
  //   0 0 1 5*0 1 2 3 6*0 5 7 8 a c d 4 6 9 b
  //   contents of rom_3 (hex, n*v repeats v):
  //   0 0 0 4 4 6*0 2 2 1 1 2 1
  //   contents of rom_4 (hex, n*v repeats v):
  //   0 1 1 4*0 1 1 11*0 1 1 1 0 0 1 1
endmodule

module registerFile (
  input  [15:0] WE,
  input  CLK,
  input  [31:0] IN0,
  output [31:0] R0OUT,
  output [31:0] R1OUT,
  output [31:0] R2OUT,
  output [31:0] R3OUT,
  output [31:0] R4OUT,
  output [31:0] R5OUT,
  output [31:0] R6OUT,
  output [31:0] R7OUT,
  output [31:0] R8OUT,
  output [31:0] R9OUT,
  output [31:0] R10OUT,
  output [31:0] R11OUT,
  output [31:0] R12OUT,
  output [31:0] R13OUT,
  output [31:0] R14OUT,
  output [31:0] R15OUT
);

  Register #(.width(32)) register_1 (.D(IN0), .en(1'b0), .clk(CLK), .Q(R0OUT));  // open: clr
  Register #(.width(32)) register_2 (.D(IN0), .en(WE[4]), .clk(CLK), .Q(R4OUT));  // open: clr
  Register #(.width(32)) register_3 (.D(IN0), .en(WE[8]), .clk(CLK), .Q(R8OUT));  // open: clr
  Register #(.width(32)) register_4 (.D(IN0), .en(WE[12]), .clk(CLK), .Q(R12OUT));  // open: clr
  Register #(.width(32)) register_5 (.D(IN0), .en(WE[1]), .clk(CLK), .Q(R1OUT));  // open: clr
  Register #(.width(32)) register_6 (.D(IN0), .en(WE[5]), .clk(CLK), .Q(R5OUT));  // open: clr
  Register #(.width(32)) register_7 (.D(IN0), .en(WE[9]), .clk(CLK), .Q(R9OUT));  // open: clr
  Register #(.width(32)) register_8 (.D(IN0), .en(WE[13]), .clk(CLK), .Q(R13OUT));  // open: clr
  Register #(.width(32)) register_9 (.D(IN0), .en(WE[2]), .clk(CLK), .Q(R2OUT));  // open: clr
  Register #(.width(32)) register_10 (.D(IN0), .en(WE[6]), .clk(CLK), .Q(R6OUT));  // open: clr
  Register #(.width(32)) register_11 (.D(IN0), .en(WE[10]), .clk(CLK), .Q(R10OUT));  // open: clr
  Register #(.width(32)) register_12 (.D(IN0), .en(WE[14]), .clk(CLK), .Q(R14OUT));  // open: clr
  Register #(.width(32)) register_13 (.D(IN0), .en(WE[3]), .clk(CLK), .Q(R3OUT));  // open: clr
  Register #(.width(32)) register_14 (.D(IN0), .en(WE[7]), .clk(CLK), .Q(R7OUT));  // open: clr
  Register #(.width(32)) register_15 (.D(IN0), .en(WE[11]), .clk(CLK), .Q(R11OUT));  // open: clr
  Register #(.width(32)) register_16 (.D(IN0), .en(WE[15]), .clk(CLK), .Q(R15OUT));  // open: clr
endmodule

module flags (
  input  [1:0] INOP,
  input  [7:0] IN0,
  input  CLK,
  output [7:0] OUT0
);

  wire comparator_1_eq;

  Comparator #(.width(2)) comparator_1 (.a(INOP), .b(2'b00), .eq(comparator_1_eq));  // open: gt, lt
  Register register_1 (.D(IN0), .en(comparator_1_eq), .clk(CLK), .Q(OUT0));  // open: clr
endmodule

module ram32 (
  input  [7:0] IN0,
  input  [7:0] IN1,
  input  [7:0] IN2,
  input  [7:0] IN3,
  input  [21:0] ADDR,
  input  [3:0] WRITE,
  input  [3:0] READ,
  input  CLK,
  output [7:0] OUT0,
  output [7:0] OUT1,
  output [7:0] OUT2,
  output [7:0] OUT3
);

  RAM #(.addrWidth(22), .asyncread("true")) ram_1 (
    .addr(ADDR), .we(WRITE[0]), .oe(READ[0]), .clk(CLK), .din(IN0), .dout(OUT0));
  RAM #(.addrWidth(22)) ram_2 (.addr(ADDR), .we(WRITE[2]), .oe(READ[2]), .clk(CLK), .din(IN2), .dout(OUT2));
  RAM #(.addrWidth(22)) ram_3 (.addr(ADDR), .we(WRITE[1]), .oe(READ[1]), .clk(CLK), .din(IN1), .dout(OUT1));
  RAM #(.addrWidth(22)) ram_4 (.addr(ADDR), .we(WRITE[3]), .oe(READ[3]), .clk(CLK), .din(IN3), .dout(OUT3));
endmodule
